# Fritzing sketch mp1 (saved by Fritzing 0.9.4)
breadboards: 1

parts:
  Part1 = Adafruit ItsyBitsy M4 [part_number="Adafruit #3800"]
  J1 = Basic Servo
  J2 = Basic Servo
  J3 = Basic Servo
  J4 = Basic Servo
  Part2 = Adafruit 1.44 inch TFT Breakout [part_number="Adafruit #2088"]
  KEYPAD1 = Membrane Matrix Keypad
  Part3 = SRF05 Ultrasonic Rangefinder

nets:
  N1: Part1.D3, Part3.Echo
  N2: Part1.D4, Part3.Trig
  N3: Part1.D9, Part2.TFTDC
  N4: Part1.D7, Part2.RESET
  N5: Part1.D5_5V, Part2.TFTCS
  N6: Part1.MISO, Part2.MISO
  N7: Part1.MOSI, Part2.MOSI
  N8: Part1.SCK, Part2.SCK
  N9: Part1.A5, KEYPAD1.2, KEYPAD1.3
  N10: Part1.A4, KEYPAD1.1
  N11: Part1.A3, J4.pulse
  N12: Part1.A2, J3.pulse
  N13: Part1.A1, J2.pulse
  N14: Part1.A0, J1.pulse
  +3V3: Part1.+3V3, Part2.+3V3, Part3.VCC
  GND: Part2.GND, Part3.GND

custom parts:
  Adafruit ItsyBitsy M4: What's smaller than a Feather but larger than a Trinket? It's an Adafruit ItsyBitsy M4 Express featuring the Microchip ATSAMD51! Small, powerful, with a ultra fast ATSAMD51 Cortex M4 processor running at 120 MHz - this microcontroller board is perfect when you want something very compact, with a ton of horsepower and a bunch of pins. This Itsy is like a bullet train, with it's 120MHz Cortex M4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
  Adafruit 1.44 inch TFT Breakout: This lovely little display breakout is the best way to add a small, colorful and bright display to any project. Since the display uses 4-wire SPI to communicate and has its own pixel-addressable frame buffer, it can be used with every kind of microcontroller. Even a very small one with low memory and few pins available! The 1.44" display has 128x128 color pixels. Unlike the low cost "Nokia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
  Membrane Matrix Keypad: Membrane Matrix 3x4 Keypad
